# Fritzing sketch TeensyBlueSmirf (saved by Fritzing 0.6.3b)
breadboards: 1

parts:
  Teensy_3_1 = Adafruit_Atmega32u4_Breakout.fzp [part_number="Freescale ARM MK20DX128"]
  Part1 = BlueSMiRF
  U1 = mystery part, 6 pins [chip_label=? spacing=300mil]
  VCC1 = 4 x AAA Battery Mount
  R1 = Resistor [tolerance=±5% resistance=10k package=THT]

nets:
  N1: Teensy_3_1.connector0, U1.pin3, VCC1.+
  N2: Teensy_3_1.connector1, Teensy_3_1.connector14, Teensy_3_1.connector22, Part1.connector15, U1.pin1, VCC1.-
  N3: Teensy_3_1.connector2, Part1.connector16
  N4: Teensy_3_1.connector3, Teensy_3_1.connector15
  N5: Teensy_3_1.connector4, Teensy_3_1.connector16
  N6: Teensy_3_1.connector5, Teensy_3_1.connector17
  N7: Teensy_3_1.connector13, Teensy_3_1.connector38, Teensy_3_1.connector40
  N8: Teensy_3_1.connector23, Part1.connector14
  N9: Teensy_3_1.connector24, Part1.connector13
  N10: Teensy_3_1.connector32, R1.Pin_0
  N11: Teensy_3_1.connector33, U1.pin4
  N12: Teensy_3_1.connector35, Teensy_3_1.connector37
  N13: Part1.connector12, Part1.connector17
  N14: U1.pin5, R1.Pin_1

notes:
  3.7 - 5.5V
  Power source
  3V Power Rail
  3.7-5.5V Power rail
  3DR Modem
