# Fritzing sketch Teensy_3_Xbee (saved by Fritzing 0.7.11b)

parts:
  U1 = XBee
  Teensy_3_1 = Adafruit_Atmega32u4_Breakout.fzp [part_number="Freescale ARM MK20DX128"]

nets:
  N1: U1.VCC, Teensy_3_1.connector2, Teensy_3_1.connector10, Teensy_3_1.connector11
  N2: U1.pin2, Teensy_3_1.connector30
  N3: U1.pin3, Teensy_3_1.connector31, Teensy_3_1.connector32
  N4: U1.GND, Teensy_3_1.connector22, Teensy_3_1.connector23
